# Fritzing sketch rotaryEncoder (saved by Fritzing 0.9.3b)

parts:
  RE1 = Rotary Encoder [package=THT]
  C1 = Capacitor [part_number=100nF package=grm43d]
  C2 = Capacitor [part_number=100nF package=grm43d]
  R1 = Resistor [tolerance=±5% resistance=10k package=THT]
  R2 = Resistor [tolerance=±5% resistance=10k package=THT]

nets:
  N1: RE1.EncoderPinA, C2.2, R1.Pin_1
  N2: RE1.EncoderPinC, C2.1
  N3: RE1.EncoderPinB, C1.1, R2.Pin_1

notes:
  TX1
  RX1
