# Fritzing sketch usb_circuit (saved by Fritzing 0.9.3b)
breadboards: 1

parts:
  JP1 = USB_MICROB_PLUG [package=micro-b-smt]
  R1 = Resistor [tolerance=±5% resistance=22 package=THT]
  R2 = Resistor [tolerance=±5% resistance=22 package=THT]
  R3 = Resistor [tolerance=±5% resistance=1.5k package=THT]

nets:
  N1: JP1.D-, R1.Pin_1
  N2: JP1.D+, R2.Pin_1, R3.Pin_1
  Gnd: JP1.GND
  USB_DM: R1.Pin_0
  USB_DP: R2.Pin_0
  3.3v: R3.Pin_0

notes:
  ! Pins are inverted l/r !
